# Fritzing sketch 06_SHIFT (saved by Fritzing 0.9.3b)
breadboards: 1

parts:
  Part1 = Adafruit Metro Mini [part_number="Adafruit #2590"]
  GND = BANANA_CONN [package=banana_conn]
  +9V = BANANA_CONN [package=banana_conn]
  IC1 = IC, DIP package, 8 pins [chip_label=LF398]
  IC2 = IC, DIP package, 8 pins [chip_label=LF398]
  IC3 = IC, DIP package, 8 pins [chip_label=LF398]
  IC4 = IC, DIP package, 8 pins [chip_label=LF398]
  IC5 = IC, DIP package, 8 pins [chip_label=LF398]
  IC6 = IC, DIP package, 8 pins [chip_label=LF398]
  IC7 = IC, DIP package, 8 pins [chip_label=LF398]
  IC8 = IC, DIP package, 8 pins [chip_label=LF398]
  C1 = Tantalum Capacitor [capacitance=0.1µF package="100 mil [THT, tantalum]"]
  C2 = Tantalum Capacitor [capacitance=0.1µF package="100 mil [THT, tantalum]"]
  C3 = Tantalum Capacitor [capacitance=0.1µF package="100 mil [THT, tantalum]"]
  C4 = Tantalum Capacitor [capacitance=0.1µF package="100 mil [THT, tantalum]"]
  C5 = Tantalum Capacitor [capacitance=0.1µF package="100 mil [THT, tantalum]"]
  C6 = Tantalum Capacitor [capacitance=0.1µF package="100 mil [THT, tantalum]"]
  C7 = Tantalum Capacitor [capacitance=0.1µF package="100 mil [THT, tantalum]"]
  C8 = Tantalum Capacitor [capacitance=0.1µF package="100 mil [THT, tantalum]"]
  C9 = Ceramic Capacitor [capacitance=0.01µF package="100 mil [THT, multilayer]"]
  C10 = Ceramic Capacitor [capacitance=0.01µF package="100 mil [THT, multilayer]"]
  C11 = Ceramic Capacitor [capacitance=0.01µF package="100 mil [THT, multilayer]"]
  C12 = Ceramic Capacitor [capacitance=0.01µF package="100 mil [THT, multilayer]"]
  C13 = Ceramic Capacitor [capacitance=0.01µF package="100 mil [THT, multilayer]"]
  C14 = Ceramic Capacitor [capacitance=0.01µF package="100 mil [THT, multilayer]"]
  C15 = Ceramic Capacitor [capacitance=0.01µF package="100 mil [THT, multilayer]"]
  C16 = Ceramic Capacitor [capacitance=0.01µF package="100 mil [THT, multilayer]"]
  C17 = Ceramic Capacitor [capacitance=0.01µF package="100 mil [THT, multilayer]"]
  C18 = Ceramic Capacitor [capacitance=0.01µF package="100 mil [THT, multilayer]"]
  C19 = Ceramic Capacitor [capacitance=0.01µF package="100 mil [THT, multilayer]"]
  C20 = Ceramic Capacitor [capacitance=0.01µF package="100 mil [THT, multilayer]"]
  C21 = Ceramic Capacitor [capacitance=0.01µF package="100 mil [THT, multilayer]"]
  C22 = Ceramic Capacitor [capacitance=0.01µF package="100 mil [THT, multilayer]"]
  C23 = Ceramic Capacitor [capacitance=0.01µF package="100 mil [THT, multilayer]"]
  J1_(INPUT_L) = BANANA_CONN [package=banana_conn]
  J2_(L_1_OUTPUT) = BANANA_CONN [package=banana_conn]
  J3_(L_2_OUTPUT) = BANANA_CONN [package=banana_conn]
  J4_(L_3_OUTPUT) = BANANA_CONN [package=banana_conn]
  J5_(L_4_OUTPUT) = BANANA_CONN [package=banana_conn]
  J6_(INPUT_R) = BANANA_CONN [package=banana_conn]
  J7_(R_1_OUTPUT) = BANANA_CONN [package=banana_conn]
  J8_(R_2_OUTPUT) = BANANA_CONN [package=banana_conn]
  J9_(R_3_OUTPUT) = BANANA_CONN [package=banana_conn]
  J10_(R_4_OUTPUT) = BANANA_CONN [package=banana_conn]
  C24 = Ceramic Capacitor [capacitance=0.01µF package="100 mil [THT, multilayer]"]

nets:
  N1: Part1.GND, GND.1, IC1.pin4, IC1.pin7, IC2.pin4, IC2.pin7, IC3.pin4, IC4.pin4, IC4.pin7, IC5.pin4, IC5.pin7, IC6.pin4, IC6.pin7, IC7.pin4, IC7.pin7, IC8.pin4, IC8.pin7, C1.-, C2.-, C3.-, C4.-, C5.-, C6.-, C7.-, C8.-, C9.0, C10.0, C11.0, C12.0, C13.0, C14.0, C15.0, C16.0, C17.0, C17.1, C18.0, C18.1, C19.0, C19.1, C20.0, C20.1, C21.0, C21.1, C22.0, C22.1, C23.0, C23.1, C24.0, C24.1
  N2: Part1.VIN, +9V.1, IC1.pin1, IC1.pin2, IC2.pin1, IC2.pin2, IC3.pin1, IC3.pin2, IC4.pin1, IC4.pin2, IC5.pin1, IC5.pin2, IC6.pin1, IC6.pin2, IC7.pin1, IC7.pin2, IC8.pin1, IC8.pin2, C9.1, C10.1, C11.1, C12.1, C13.1, C14.1, C15.1, C16.1
  N3: IC1.pin3, J1_(INPUT_L).1
  N4: IC1.pin5, IC2.pin3, J2_(L_1_OUTPUT).1
  N5: IC1.pin6, C1.+
  N6: IC2.pin5, IC3.pin3, J3_(L_2_OUTPUT).1
  N7: IC2.pin6, C2.+
  N8: IC3.pin5, IC4.pin3, J4_(L_3_OUTPUT).1
  N9: IC3.pin6, C3.+
  N10: IC4.pin5, J5_(L_4_OUTPUT).1
  N11: IC4.pin6, C4.+
  N12: IC5.pin3, J6_(INPUT_R).1
  N13: IC5.pin5, IC6.pin3, J7_(R_1_OUTPUT).1
  N14: IC5.pin6, C5.+
  N15: IC6.pin5, IC7.pin3, J8_(R_2_OUTPUT).1
  N16: IC6.pin6, C6.+
  N17: IC7.pin5, IC8.pin3, J9_(R_3_OUTPUT).1
  N18: IC7.pin6, C7.+
  N19: IC8.pin5, J10_(R_4_OUTPUT).1
  N20: IC8.pin6, C8.+

notes:
  06 SHIFT, Shelfisizer Module #6: Dual 4-Stage Analog Shift Register -rld, 0.1b

custom parts:
  Adafruit Metro Mini: We sure love the ATmega328 here at Adafruit, and we use them a lot for our own projects. The processor has plenty of GPIO, Analog inputs, hardware UART SPI and I2C, timers and PWM galore - just enough for most simple projects. When we need to go small, we use a Pro Trinket 3V or 5V, but if you want to have USB-to-Serial built in, we reach for an Adafruit METRO Mini. METRO Mini is the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
